# Fritzing sketch train_system (saved by Fritzing 0.9.4)
breadboards: 1

parts:
  元件1 = Arduino Uno (Rev3)
  LED1 = LED - 5mm [color="Red (633nm)" package="5 mm [THT]"]
  LED2 = LED - 5mm [color="Yellow (595nm)" package="5 mm [THT]"]
  LED3 = LED - 5mm [color="Green (570nm)" package="5 mm [THT]"]
  R1 = Resistor [tolerance=±5% resistance=1k package="2010 [SMD]"]
  R2 = Resistor [tolerance=±5% resistance=1k package="2010 [SMD]"]
  R3 = Resistor [tolerance=±5% resistance=1k package="2010 [SMD]"]
  R4 = Resistor [tolerance=±5% resistance=1k package="2010 [SMD]"]
  S1 = Pushbutton [package="[THT]"]
  SP1 = SPEAKER [package=pcb_mount_speaker]

nets:
  N1: 元件1.D8, SP1.-
  N2: 元件1.D12/MISO, R4.Pin_0, S1.Pin_1, S1.Pin_2
  N3: 元件1.D2, R3.Pin_1
  N4: 元件1.D3_PWM, R2.Pin_1
  N5: 元件1.D4, R1.Pin_1
  N6: 元件1.3V3, R4.Pin_1, S1.Pin_3, S1.Pin_4
  N7: 元件1.GND, LED1.anode, LED2.anode, LED3.anode, SP1.+
  N8: LED1.cathode, R1.Pin_0
  N9: LED2.cathode, R2.Pin_0
  N10: LED3.cathode, R3.Pin_0
